// Logisim project Afficheur_7_Digit.circ as structural Verilog: 1 circuit, main circuit main
module main (
  input  [3:0] in_1
);

  wire _0_out, _1_out, _2_out, _3_out, _4_out, _5_out, _6_out, _7_out, _8_out, _9_out, not_1_out, not_2_out,
       not_3_out, not_4_out, not_5_out, not_6_out, not_7_out, not_8_out, not_9_out, not_10_out, not_11_out,
       not_12_out, not_13_out, not_14_out, not_15_out, not_16_out, not_17_out, not_18_out, not_19_out,
       not_20_out, not_21_out, not_22_out, not_23_out, not_24_out, not_25_out, or_1_out, or_2_out, or_3_out,
       or_4_out, or_5_out, or_6_out, or_7_out;

  // Probe on in_1
  not not_1 (not_1_out, in_1[0]);
  not not_2 (not_2_out, in_1[2]);
  not not_3 (not_3_out, in_1[3]);
  not not_4 (not_4_out, in_1[1]);
  not not_5 (not_5_out, in_1[2]);
  not not_6 (not_6_out, in_1[3]);
  not not_7 (not_7_out, in_1[2]);
  not not_8 (not_8_out, in_1[3]);
  not not_9 (not_9_out, in_1[0]);
  not not_10 (not_10_out, in_1[1]);
  not not_11 (not_11_out, in_1[3]);
  not not_12 (not_12_out, in_1[1]);
  not not_13 (not_13_out, in_1[3]);
  not not_14 (not_14_out, in_1[0]);
  not not_15 (not_15_out, in_1[3]);
  not not_16 (not_16_out, in_1[3]);
  not not_17 (not_17_out, in_1[0]);
  not not_18 (not_18_out, in_1[0]);
  not not_19 (not_19_out, in_1[2]);
  not not_20 (not_20_out, in_1[1]);
  not not_21 (not_21_out, in_1[2]);
  not not_22 (not_22_out, in_1[0]);
  not not_23 (not_23_out, in_1[1]);
  not not_24 (not_24_out, in_1[2]);
  not not_25 (not_25_out, in_1[3]);
  and _1 (_1_out, in_1[0], not_4_out, not_5_out, not_6_out);
  and _2 (_2_out, not_1_out, in_1[1], not_2_out, not_3_out);
  and _3 (_3_out, in_1[0], in_1[1], not_7_out, not_8_out);
  and _4 (_4_out, not_9_out, not_10_out, in_1[2], not_11_out);
  and _5 (_5_out, in_1[0], not_12_out, in_1[2], not_13_out);
  and _6 (_6_out, not_14_out, in_1[1], in_1[2], not_15_out);
  and _7 (_7_out, in_1[2], in_1[1], in_1[0], not_16_out);
  and _8 (_8_out, not_17_out, not_18_out, not_19_out, in_1[3]);
  and _9 (_9_out, in_1[0], not_20_out, not_21_out, in_1[3]);
  and _0 (_0_out, not_22_out, not_23_out, not_24_out, not_25_out);
  or or_1 (or_1_out, _1_out, _2_out, _3_out, _4_out, _7_out, _8_out, _9_out, _0_out);
  or or_2 (or_2_out, _2_out, _3_out, _5_out, _6_out, _7_out, _8_out, _9_out, _0_out);
  or or_3 (or_3_out, _4_out, _5_out, _6_out, _8_out, _9_out, _0_out);
  or or_4 (or_4_out, _2_out, _3_out, _4_out, _5_out, _6_out, _8_out, _9_out);
  or or_5 (or_5_out, _2_out, _6_out, _8_out, _0_out);
  or or_6 (or_6_out, _2_out, _3_out, _5_out, _6_out, _8_out, _9_out, _0_out);
  or or_7 (or_7_out, _1_out, _3_out, _4_out, _5_out, _6_out, _7_out, _8_out, _9_out, _0_out);
  _7_Segment_Display u_7_segment_display_1 (
    .g(or_4_out), .f(or_3_out), .a(or_2_out), .b(or_1_out), .e(or_5_out), .d(or_6_out), .c(or_7_out));  // open: dp
endmodule
